# Fritzing sketch Tisch-komplett (saved by Fritzing 1.0.6)

parts:
  U1 = Spannungsversorgung 230V [chip_label="Spannungsversorgung 230V" package="SIP (Single Inline) [THT]"]
  U4 = 24V Netzteil [chip_label="24V Netzteil" package="SIP (Single Inline) [THT]"]
  U3 = 12V Netzteil [chip_label="12V Netzteil" package="SIP (Single Inline) [THT]"]
  U5 = 5V Netzteil [chip_label="5V Netzteil" package="SIP (Single Inline) [THT]"]
  M1 = 1 chan 5v relay module
  U6 = 5V Netzteil [chip_label="5V Netzteil" package="SIP (Single Inline) [THT]"]
  J1 = Wago 221-413
  J2 = Wago 221-413
  U7 = Spannungsversorgung 230V [chip_label="Spannungsversorgung 230V" package="SIP (Single Inline) [THT]"]
  A1 = Raspberry Pi 5
  U23 = Module 4 Relais 5V [package="Module 4 Relais 5V"]
  U24 = 12V Netzteil [chip_label="12V Netzteil" package="SIP (Single Inline) [THT]"]
  Kühler = SIP - 2 pins [chip_label=Kühler package="SIP (Single Inline) [THT]"]
  Heizstab = 230V Spannungsabnehmer [chip_label=230V-Spannungsabnehmer package="SIP (Single Inline) [THT]"]
  U25 = ESP32S-HiLetgo [part_number=ESP32S-HiLetgo]
  Pumpe = IC, SIP package, 5 pins [chip_label=230V-Spannungsabnehmer]
  J7 = Wago 221-415
  J8 = Wago 221-415
  J9 = Wago 221-415
  J10 = Wago 221-415
  J11 = Wago 221-415
  J12 = Wago 221-415
  J13 = Wago 221-413
  Nebelmaschine = 230V Spannungsabnehmer [chip_label=230V-Spannungsabnehmer package="SIP (Single Inline) [THT]"]
  J14 = Wago 221-415
  J15 = Wago 221-415
  J16 = Wago 221-412
  U27 = 3-Wege-Ventil [chip_label=Ventil-3-Wege package="SIP (Single Inline) [THT]"]
  J17 = Wago 221-412
  J18 = Wago 221-412
  U28 = 3-Wege-Ventil [chip_label=Ventil-3-Wege package="SIP (Single Inline) [THT]"]
  U29 = Temperatursensor 10k [chip_label="Temperatursensor 10k" package="SIP (Single Inline) [THT]"]
  J19 = Wago 221-413
  J20 = Wago 221-415
  J21 = Wago 221-413
  R1 = Resistor [tolerance=±5% resistance=10k power=0.25W package=THT]
  J22 = Wago 221-415
  J23 = Wago 221-413
  J24 = Wago 221-413
  J25 = Wago 221-413
  J26 = Wago 221-415
  U30 = ESP32S-HiLetgo [part_number=ESP32S-HiLetgo]
  J27 = Wago 221-412
  J28 = Wago 221-412
  J29 = Wago 221-415
  J30 = Wago 221-412
  J31 = Wago 221-412
  J32 = Wago 221-412
  J33 = Wago 221-412
  J34 = Wago 221-412
  S1 = Pushbutton [package="[THT]"]
  J35 = Wago 221-412
  J36 = Wago 221-415
  J37 = Wago 221-413
  IC6 = SIP - 2 pins [chip_label="2 Pin Connector" package="SIP (Single Inline) [THT]"]
  IC7 = SIP - 2 pins [chip_label="2 Pin Connector" package="SIP (Single Inline) [THT]"]
  U14 = Spannungsversorgung 230V [chip_label="Spannungsversorgung 230V" package="SIP (Single Inline) [THT]"]
  J3 = Wago 221-413
  U13 = Spannungsversorgung 230V [chip_label="Spannungsversorgung 230V" package="SIP (Single Inline) [THT]"]
  J6 = Wago 221-413
  IC3 = IC, SIP package, 3 pins [chip_label=Windrad]
  U8 = Spannungsversorgung 230V [chip_label="Spannungsversorgung 230V" package="SIP (Single Inline) [THT]"]
  IC1 = IC, SIP package, 5 pins [chip_label=MFC]
  IC4 = IC, DIP package, 6 pins [chip_label=Windrad-Connector]
  IC5 = IC, SIP package, 3 pins [chip_label=Windrad]
  IC2 = IC, DIP package, 6 pins [chip_label=Windrad-Connector]
  J5 = Wago 221-413
  U21 = Ventil 12V [chip_label="Ventil 12V" package="SIP (Single Inline) [THT]"]
  IC8 = SIP - 2 pins [chip_label="2 Pin Connector" package="SIP (Single Inline) [THT]"]  # not connected
  IC9 = SIP - 2 pins [chip_label="2 Pin Connector" package="SIP (Single Inline) [THT]"]  # not connected
  IC10 = SIP - 2 pins [chip_label="2 Pin Connector" package="SIP (Single Inline) [THT]"]
  IC11 = SIP - 2 pins [chip_label="2 Pin Connector" package="SIP (Single Inline) [THT]"]
  IC12 = SIP - 2 pins [chip_label="2 Pin Connector" package="SIP (Single Inline) [THT]"]
  IC13 = SIP - 2 pins [chip_label="2 Pin Connector" package="SIP (Single Inline) [THT]"]
  IC14 = SIP - 2 pins [chip_label="2 Pin Connector" package="SIP (Single Inline) [THT]"]
  IC15 = SIP - 2 pins [chip_label="2 Pin Connector" package="SIP (Single Inline) [THT]"]
  J38 = Wago 221-413
  J39 = Wago 221-413
  J40 = Wago 221-413
  J41 = Wago 221-413
  J42 = Wago 221-412
  J43 = Wago 221-412
  J44 = Wago 221-412
  J45 = Wago 221-415
  J46 = Wago 221-412
  J47 = Wago 221-412
  Kühler1 = SIP - 2 pins [chip_label=Kühler package="SIP (Single Inline) [THT]"]
  J52 = Wago 221-413
  J53 = Wago 221-413
  J54 = Wago 221-413
  J55 = Wago 221-413
  J56 = Wago 221-413
  U31 = 12V Netzteil [chip_label="12V Netzteil" package="SIP (Single Inline) [THT]"]
  U32 = Module 4 Relais 5V [package="Module 4 Relais 5V"]
  J57 = Wago 221-415
  J58 = Wago 221-412
  J59 = Wago 221-412
  U33 = ESP32S-HiLetgo [part_number=ESP32S-HiLetgo]
  U34 = Module 4 Relais 5V [package="Module 4 Relais 5V"]
  A2 = Mini RS232 to ttl module
  J60 = Wago 221-415
  J61 = Wago 221-413
  J62 = Wago 221-413
  Heizstab1 = 230V Spannungsabnehmer [chip_label=230V-Spannungsabnehmer package="SIP (Single Inline) [THT]"]
  J63 = Wago 221-415
  J64 = Wago 221-415
  J65 = Wago 221-415
  U35 = 3-Wege-Ventil [chip_label=Ventil-3-Wege package="SIP (Single Inline) [THT]"]
  J66 = Wago 221-412
  J67 = Wago 221-412
  U36 = 3-Wege-Ventil [chip_label=Ventil-3-Wege package="SIP (Single Inline) [THT]"]
  Pumpe_2 = 230V Spannungsabnehmer [chip_label=230V-Spannungsabnehmer package="SIP (Single Inline) [THT]"]  # not connected
  Zünder = 230V Spannungsabnehmer [chip_label=230V-Spannungsabnehmer package="SIP (Single Inline) [THT]"]
  U37 = Temperatursensor 10k [chip_label="Temperatursensor 10k" package="SIP (Single Inline) [THT]"]
  J68 = Wago 221-415
  J69 = Wago 221-415
  J70 = Wago 221-413
  J71 = Wago 221-413
  J72 = Wago 221-413
  R2 = Resistor [tolerance=±5% power=0.25W resistance=220 package=THT]
  Pumpe2 = IC, SIP package, 5 pins [chip_label=230V-Spannungsabnehmer]
  U38 = ESP32S-HiLetgo [part_number=ESP32S-HiLetgo]  # not connected
  S2 = H-Bridge with L298N
  IC16 = SIP - 2 pins [chip_label=Zug package="SIP (Single Inline) [THT]"]
  A3 = ESP32 devkit 38p expansion board
  IC17 = IC, SIP package, 3 pins [chip_label=Windrad]
  IC18 = IC, DIP package, 6 pins [chip_label=Windrad-Connector]
  IC19 = IC, SIP package, 3 pins [chip_label=Windrad]
  IC20 = IC, DIP package, 6 pins [chip_label=Windrad-Connector]
  IC21 = IC, SIP package, 3 pins [chip_label=Windrad]
  IC22 = IC, DIP package, 6 pins [chip_label=Windrad-Connector]
  IC23 = IC, SIP package, 3 pins [chip_label=Windrad]
  IC24 = IC, DIP package, 6 pins [chip_label=Windrad-Connector]

nets:
  N1: U1.Phase, M1.pin_5, U6.Phase
  N2: U1.Neutral, U4.Neutral, U3.Neutral, U5.Neutral, U6.Neutral, J2.Pin_1, J2.Pin_3, U7.Neutral, U24.Neutral, Heizstab.Neutral, Pumpe.pin2, J7.Pin_1, J7.Pin_2, J7.Pin_3, J7.Pin_4, J7.Pin_5, J9.Pin_1, J9.Pin_2, J9.Pin_4, J9.Pin_5, Nebelmaschine.Neutral, J15.Pin_1, J15.Pin_2, J15.Pin_3, J15.Pin_5, U27.Neutral, U28.Neutral, J31.Pin_1, J31.Pin_2
  N3: U1.Schutz, U4.Schutz, U3.Schutz, U5.Schutz, U6.Schutz, U7.Schutz, U24.Schutz, Heizstab.Schutz, Pumpe.pin3, J10.Pin_1, J10.Pin_2, J10.Pin_4, J10.Pin_5, J11.Pin_1, J11.Pin_2, J11.Pin_3, J11.Pin_4, J11.Pin_5, J13.Pin_1, J13.Pin_3, Nebelmaschine.Schutz, J16.Pin_1, J16.Pin_2, J30.Pin_1, J30.Pin_2
  N4: U4.Phase, U3.Phase, U5.Phase, M1.pin_4, J1.Pin_1, J1.Pin_3, U7.Phase, U23.K2-NF, U23.K3-NF, U23.K4-NF, U24.Phase, Pumpe.pin1, J8.Pin_1, J8.Pin_2, J8.Pin_4, J8.Pin_5, J12.Pin_1, J12.Pin_2, J12.Pin_3, J12.Pin_4, J12.Pin_5, Nebelmaschine.Phase, J14.Pin_1, J14.Pin_4, J14.Pin_5, U27.Phase, U28.Phase, J29.Pin_1, J29.Pin_2, J29.Pin_3, J29.Pin_4, J29.Pin_5
  N5: U4.24V+, J24.Pin_1, J24.Pin_2, J24.Pin_3, IC6.pin1
  GND: U4.24V-_COM, U3.12V-_COM, U5.12V-_COM, U23.GND, U25.GND, U29.pin1, J20.Pin_1, J20.Pin_2, J20.Pin_3, J20.Pin_4, J22.Pin_1, J22.Pin_2, J22.Pin_3, J22.Pin_4, J22.Pin_5, J23.Pin_1, J23.Pin_2, J23.Pin_3, U30.GND, J28.Pin_1, J28.Pin_2, IC7.pin2
  N6: U3.12V+, J25.Pin_1, J25.Pin_2, J25.Pin_3, IC6.pin2
  VIN: U5.12V+, U23.VCC, U25.VIN, J21.Pin_1, J21.Pin_2, J21.Pin_3, J26.Pin_1, J26.Pin_2, J26.Pin_3, J26.Pin_4, J26.Pin_5, U30.VIN, J27.Pin_1, J27.Pin_2, IC7.pin1
  N7: M1.pin_1, M1.pin_2, U6.12V+, U6.12V-_COM, A1.5V, A1.Fan-5V, S1.Pin_3, J36.Pin_1, J36.Pin_2, J36.Pin_3, J36.Pin_5, J37.Pin_1, J37.Pin_2, J37.Pin_3
  N8: M1.pin_3, S1.Pin_1, J35.Pin_1, J35.Pin_2
  N9: U23.IN1, U25.GPIO26
  N10: U23.IN2, U25.GPIO25
  N11: U23.IN3, U25.GPIO33
  N12: U23.IN4, U25.GPIO32
  N13: U23.K1-NF, U24.12V+
  N14: U23.K1-NO, Kühler.pin1, J33.Pin_1, J33.Pin_2
  N15: U23.K2-NO, Heizstab.Phase
  N16: U23.K3-NO, U27.Control, J18.Pin_1, J18.Pin_2
  N17: U23.K4-NO, J17.Pin_1, J17.Pin_2, U28.Control
  N18: U24.12V-_COM, Kühler.pin2, J32.Pin_1, J32.Pin_2, J34.Pin_1, J34.Pin_2
  N19: U25.3.3, R1.Pin_0
  N20: U25.GPIO34, U29.pin2, J19.Pin_1, J19.Pin_2, J19.Pin_3, R1.Pin_1
  N21: U14.Phase, J52.Pin_1, J52.Pin_2, J52.Pin_3, U31.Phase, U34.K1-NF, U34.K2-NF, U34.K3-NF, U34.K4-NF, J60.Pin_1, J60.Pin_2, J60.Pin_3, J60.Pin_4, J60.Pin_5, J65.Pin_1, J65.Pin_2, J65.Pin_3, J65.Pin_4, J65.Pin_5, U35.Phase, U36.Phase, Pumpe2.pin1
  N22: U14.Neutral, J53.Pin_1, J53.Pin_2, J53.Pin_3, U31.Neutral, J61.Pin_1, J61.Pin_2, J61.Pin_3, Heizstab1.Neutral, J64.Pin_1, J64.Pin_2, J64.Pin_3, J64.Pin_4, J64.Pin_5, U35.Neutral, U36.Neutral, Zünder.Phase, Pumpe2.pin2
  N23: U14.Schutz, J54.Pin_1, J54.Pin_2, J54.Pin_3, U31.Schutz, J62.Pin_1, J62.Pin_2, J62.Pin_3, Heizstab1.Schutz, J63.Pin_1, J63.Pin_2, J63.Pin_3, J63.Pin_5, Pumpe2.pin3
  N24: J3.Pin_1, J3.Pin_3, U13.Phase, U8.Phase
  N25: U13.Neutral, U8.Neutral, J5.Pin_1, J5.Pin_3
  N26: U13.Schutz, J6.Pin_1, J6.Pin_3, U8.Schutz
  N27: IC3.pin1, IC2.pin6
  N28: IC3.pin2, IC2.pin5
  N29: IC3.pin3, IC2.pin4
  N30: IC1.pin1, U32.K3-NO
  GND_2: IC1.pin2, IC1.pin5, U21.GND, IC11.pin2, IC13.pin2, IC14.pin2, J47.Pin_1, J47.Pin_2, Kühler1.pin2, J55.Pin_1, J55.Pin_2, J55.Pin_3, U31.12V-_COM, U32.GND, J57.Pin_1, J57.Pin_2, J57.Pin_3, J57.Pin_4, J57.Pin_5, J59.Pin_1, J59.Pin_2, U33.GND, U34.GND, A2.Pin_1, A2.Pin_5, U37.pin1, J68.Pin_1, J68.Pin_2, J68.Pin_3, J68.Pin_4, J68.Pin_5, J70.Pin_1, J70.Pin_2, J70.Pin_3, Pumpe2.pin5, S2.GND, S2.IN2, A3.Pin_35, A3.Pin_52, A3.Pin_54, A3.Pin_136
  N31: IC1.pin3, A2.Pin_8
  N32: IC1.pin4, A2.Pin_7
  N33: IC4.pin4, IC5.pin3
  N34: IC4.pin5, IC5.pin2
  N35: IC4.pin6, IC5.pin1
  N36: U21.12V+, U32.K1-NO
  N37: U21.Schutz, J58.Pin_1, J58.Pin_2
  N38: IC10.pin1, J40.Pin_1, J40.Pin_3, J43.Pin_1, J43.Pin_2
  N39: IC10.pin2, IC12.pin2, IC15.pin2, J38.Pin_1, J38.Pin_3, J45.Pin_1, J45.Pin_3, J45.Pin_4, J45.Pin_5
  N40: IC11.pin1, U32.K1-NF
  N41: IC12.pin1, J41.Pin_1, J41.Pin_3, J42.Pin_1, J42.Pin_2
  N42: IC13.pin1, U32.K3-NF
  VCC: IC14.pin1, J56.Pin_1, J56.Pin_2, J56.Pin_3, U32.VCC, U32.K4-NF, U33.VIN, U34.VCC, J69.Pin_1, J69.Pin_2, J69.Pin_3, J69.Pin_4, J69.Pin_5, S2.IN1, A3.Pin_17, A3.Pin_56, A3.Pin_57, A3.Pin_98
  N43: IC15.pin1, J39.Pin_1, J39.Pin_3, J44.Pin_1, J44.Pin_2
  N44: J46.Pin_1, J46.Pin_2, Kühler1.pin1, U32.K2-NO
  N45: U31.12V+, U32.K2-NF, S2.12V
  N46: U32.IN1, U33.GPIO32
  N47: U32.IN2, U33.GPIO33
  N48: U32.IN3, U33.GPIO25
  N49: U32.IN4, U33.GPIO26
  N50: U32.K4-NO, Pumpe2.pin4
  N51: U33.3.3, A2.Pin_2, J72.Pin_1, J72.Pin_2, J72.Pin_3, R2.Pin_1
  N52: U33.GPIO34, U37.pin2, J71.Pin_1, J71.Pin_2, J71.Pin_3, R2.Pin_0
  N53: U33.GPIO16, A2.Pin_4
  N54: U33.GPIO17, A2.Pin_3
  N55: U33.GPIO19, U34.IN1
  N56: U33.GPIO21, U34.IN2
  N57: U33.GPIO22, U34.IN3
  N58: U33.GPIO23, U34.IN4
  N59: U34.K1-NO, J67.Pin_1, J67.Pin_2, U36.Control
  N60: U34.K2-NO, U35.Control, J66.Pin_1, J66.Pin_2
  N61: U34.K3-NO, Heizstab1.Phase
  N62: U34.K4-NO, Zünder.Neutral
  N63: S2.ENA, A3.Pin_8
  N64: S2.M1-01, IC16.pin2
  N65: S2.M1-02, IC16.pin1
  N66: IC17.pin1, IC18.pin6
  N67: IC17.pin2, IC18.pin5
  N68: IC17.pin3, IC18.pin4
  N69: IC19.pin1, IC20.pin6
  N70: IC19.pin2, IC20.pin5
  N71: IC19.pin3, IC20.pin4
  N72: IC21.pin1, IC22.pin6
  N73: IC21.pin2, IC22.pin5
  N74: IC21.pin3, IC22.pin4
  N75: IC23.pin1, IC24.pin6
  N76: IC23.pin2, IC24.pin5
  N77: IC23.pin3, IC24.pin4

custom parts:
  Spannungsversorgung 230V: A SIP stand-in part for whatever you want. With 3 pins on a 300 mil single inline package (SIP) footprint.
  24V Netzteil: A SIP stand-in part for whatever you want. With 5 pins on a 300 mil single inline package (SIP) footprint.
  12V Netzteil: A SIP stand-in part for whatever you want. With 5 pins on a 300 mil single inline package (SIP) footprint.
  5V Netzteil: A SIP stand-in part for whatever you want. With 5 pins on a 300 mil single inline package (SIP) footprint.
  1 chan 5v relay module: 1 Channel 5V Relay Module Board Shield with Optocoupler Support High and Low Level Trigger for Arduino.
  Wago 221-413: Wago 221-413 3 position splicing connector 12AWG.
  Raspberry Pi 5: The RPi5, a faster version of the awesome Raspberry Pi4B ARM Board with 40 pin gpio.
  Module 4 Relais 5V: Module 4 Relais 5V 4x SPD-06VDC-SD-C
  230V Spannungsabnehmer: A SIP stand-in part for whatever you want. With 3 pins on a 300 mil single inline package (SIP) footprint.
  ESP32S-HiLetgo: HiLetgo ESP-WROOM-32 ESP32 ESP-32S Development Board 2.4GHz Dual-Mode WiFi + Bluetooth Dual Cores Microcontroller The ESP32 integrated with Antenna switches, RF Balun, power amplifiers, low-noise amplifiers, filters, and management modules, and the entire solution occupies the least area of PCB. 2.4 GHz Wi-Fi plus Bluetooth dual-mode chip, with TSMC Ultra-low power consumption 40nm technology,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
  Wago 221-415: Wago 221-415 5 position splicing connector 12AWG.
  Wago 221-412: Wago 221-412 2 position splicing connector 12AWG.
  3-Wege-Ventil: A SIP stand-in part for whatever you want. With 3 pins on a 300 mil single inline package (SIP) footprint.
  Temperatursensor 10k: A SIP stand-in part for whatever you want. With 2 pins on a 300 mil single inline package (SIP) footprint.
  Ventil 12V: A SIP stand-in part for whatever you want. With 3 pins on a 300 mil single inline package (SIP) footprint.
  Mini RS232 to ttl module: Mini RS232 to ttl module.
  H-Bridge with L298N: h-bridge
  ESP32 devkit 38p expansion board: Upgraded ESP32 38P Development ESP32-DevKitC-32 ESP-WROOM-32 Expansion Board.
