# Fritzing sketch gaskraftwerk (saved by Fritzing 0.9.5d)
breadboards: 1

parts:
  U1 = ESP32S-HiLetgo [part_number=ESP32S-HiLetgo]
  M1 = 1 chan 5v relay module
  J2 = Power Jack [package=power_jack_combo]
  M2 = 1 chan 5v relay module
  M3 = 1 chan 5v relay module
  M4 = 1 chan 5v relay module
  JP1 = Header 6 [package=1x06-smd]
  J3 = Dagu DGServo 9g header (male) [package=THT]
  J4 = Dagu DGServo 9g header (male) [package=THT]
  J5 = Dagu DGServo 9g header (male) [package=THT]
  J6 = Dagu DGServo 9g header (male) [package=THT]
  J7 = Dagu DGServo 9g header (male) [package=THT]
  J8 = Dagu DGServo 9g header (male) [package=THT]
  J9 = Dagu DGServo 9g header (male) [package=THT]
  J10 = Dagu DGServo 9g header (male) [package=THT]
  J11 = Dagu DGServo 9g header (male) [package=THT]
  J12 = Dagu DGServo 9g header (male) [package=THT]
  J13 = Dagu DGServo 9g header (male) [package=THT]
  J14 = Dagu DGServo 9g header (male) [package=THT]
  JP2 = Header 6 [package=1x06-smd]
  JP3 = Header 6 [package=1x06-smd]
  JP4 = Header 6 [package=1x06-smd]
  J15 = JST-VHR-3N [part_number=JST-VHR-3N package=THT]
  M5 = 1 chan 5v relay module
  JP5 = Header 6 [package=1x06-smd]
  J16 = Dagu DGServo 9g header (male) [package=THT]
  J17 = Dagu DGServo 9g header (male) [package=THT]
  J18 = Dagu DGServo 9g header (male) [package=THT]
  R1 = Resistor [tolerance=±5% resistance=1k package="0603 [SMD]"]
  R2 = Resistor [tolerance=±5% resistance=1k package="0603 [SMD]"]
  R3 = Resistor [tolerance=±5% resistance=1k package="0603 [SMD]"]
  R4 = Resistor [tolerance=±5% resistance=1k package="0603 [SMD]"]
  R5 = Resistor [tolerance=±5% resistance=1k package="0603 [SMD]"]
  J19 = Power Jack [package=power_jack_combo]
  J20 = Power Jack [package=power_jack_combo]
  M6 = 1 chan 5v relay module
  JP6 = Header 6 [package=1x06-smd]
  X1 = DB9 Connector [package=db9]

nets:
  N1: U1.EN, R1.Pin_1
  N2: U1.GPIO36, R2.Pin_1
  N3: U1.GPIO39, R3.Pin_1
  N4: U1.GPIO34, R4.Pin_1
  N5: U1.GPIO35, R5.Pin_1
  N6: U1.GPIO33, M6.pin_3
  N7: U1.GPIO11, M1.pin_2, J2.GNDBREAK, M2.pin_2, M3.pin_2, M4.pin_2, M5.pin_2
  N8: U1.GPIO1, X1.7
  N9: U1.GPIO22, X1.6
  N10: M1.pin_1, J2.GND, M2.pin_1, M3.pin_1, M4.pin_1, M5.pin_1
  N11: M1.pin_3, R1.Pin_0
  N12: M1.pin_5, J3.Vcc
  N13: M1.pin_6, JP1.4
  N14: M2.pin_3, R2.Pin_0
  N15: M2.pin_5, J4.Vcc
  N16: M2.pin_6, JP2.4
  N17: M3.pin_3, R4.Pin_0
  N18: M3.pin_5, J5.Vcc
  N19: M3.pin_6, JP3.4
  N20: M4.pin_3, R3.Pin_0
  N21: M4.pin_5, J6.Vcc
  N22: M4.pin_6, JP4.4
  N23: JP1.5, J7.Vcc
  N24: JP1.6, J14.Vcc
  N25: J3.gnd, J15.pin3, J15.pin_6
  N26: J3.pulse, J4.gnd
  N27: J4.pulse, J6.gnd
  N28: J5.gnd, J6.pulse
  N29: J5.pulse, J18.gnd
  N30: J7.gnd, J15.pin2, J15.pin_5
  N31: J7.pulse, J8.gnd
  N32: J8.Vcc, JP2.5
  N33: J8.pulse, J9.gnd
  N34: J9.Vcc, JP4.5
  N35: J9.pulse, J10.gnd
  N36: J10.Vcc, JP3.5
  N37: J10.pulse, J16.gnd
  N38: J11.gnd, J14.pulse
  N39: J11.Vcc, JP2.6
  N40: J11.pulse, J12.gnd
  N41: J12.Vcc, JP4.6
  N42: J12.pulse, J13.gnd
  N43: J13.Vcc, JP3.6
  N44: J13.pulse, J17.gnd
  N45: J14.gnd, J15.pin1, J15.pin_4
  N46: M5.pin_3, R5.Pin_0
  N47: M5.pin_5, J18.Vcc
  N48: M5.pin_6, JP5.4
  N49: JP5.5, J16.Vcc
  N50: JP5.6, J17.Vcc
  N51: J19.GND, JP6.3
  N52: J19.GNDBREAK, M6.pin_5
  N53: J20.GND, X1.3
  N54: J20.GNDBREAK, X1.2
  N55: M6.pin_6, JP6.1

notes:
  Zünder
  Ventil Kühlung
  Ventil Turbine
  Pumpe
  Heizstab
  230v AC
  5v
  12v
  24v

custom parts:
  ESP32S-HiLetgo: HiLetgo ESP-WROOM-32 ESP32 ESP-32S Development Board 2.4GHz Dual-Mode WiFi + Bluetooth Dual Cores Microcontroller The ESP32 integrated with Antenna switches, RF Balun, power amplifiers, low-noise amplifiers, filters, and management modules, and the entire solution occupies the least area of PCB. 2.4 GHz Wi-Fi plus Bluetooth dual-mode chip, with TSMC Ultra-low power consumption 40nm technology,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
  1 chan 5v relay module: 1 Channel 5V Relay Module Board Shield with Optocoupler Support High and Low Level Trigger for Arduino.

// code stored in the sketch: sketch_jul20a.ino
const int ledPins[] = {26, 27};
const int motorPin = 22;
const int buttonPin = 21;

bool isRunning = false;
bool lastStableButtonState = HIGH;
bool lastReadButtonState = HIGH;
unsigned long lastDebounceTime = 0;
const unsigned long debounceDelay = 50;

const unsigned long blinkOnTime = 300;
const unsigned long blinkOffTime = 1000;

unsigned long lastBlinkTime = 0;
bool ledState = false;

void setup() {
  Serial.begin(115200);

  pinMode(buttonPin, INPUT_PULLUP);
  pinMode(motorPin, OUTPUT);
  digitalWrite(motorPin, LOW);

  for (int i = 0; i < sizeof(ledPins) / sizeof(ledPins[0]); i++) {
    pinMode(ledPins[i], OUTPUT);
    digitalWrite(ledPins[i], LOW);
  }
}

void loop() {
  // --- Button-Handling ---
  bool reading = digitalRead(buttonPin);

  if (reading != lastReadButtonState) {
    lastDebounceTime = millis();  // reset debounce timer
  }

  if ((millis() - lastDebounceTime) > debounceDelay) {
    if (reading != lastStableButtonState) {
      lastStableButtonState = reading;

      if (reading == LOW) {
        // nur bei Wechsel auf gedrückt
        isRunning = !isRunning;
        Serial.println(isRunning ? "Anlage EIN" : "Anlage AUS");
      }
    }
  }

  lastReadButtonState = reading;

  // --- Windradsteuerung ---
  if (isRunning) {
    digitalWrite(motorPin, HIGH);

    // Synchrones Blinken
    unsigned long now = millis();
    unsigned long interval = ledState ? blinkOnTime : blinkOffTime;

    if (now - lastBlinkTime >= interval) {
      lastBlinkTime = now;
      ledState = !ledState;

      for (int i = 0; i < sizeof(ledPins) / sizeof(ledPins[0]); i++) {
        digitalWrite(ledPins[i], ledState ? HIGH : LOW);
      }
    }

  } else {
    // Alles aus
    digitalWrite(motorPin, LOW);
    for (int i = 0; i < sizeof(ledPins) / sizeof(ledPins[0]); i++) {
      digitalWrite(ledPins[i], LOW);
    }
  }
}
